# Fritzing sketch schematic (saved by Fritzing 0.9.5d)

parts:
  U1 = L9110 H-bridge module [part_number="L9110 H-bridge"]
  Part2 = FC-03 [chip_label=FC-03]
  Part3 = FC-03 [chip_label=FC-03]
  M2 = DC Motor
  M3 = DC Motor
  M4 = DOIT Esp32 DevKit v1 (30 pins long, 11 pins width) [part_number=ESP32S-PIN30]
  Part4 = InvenSense MPU6050
  J18 = double row rounded female pin header, 8 pins [form="♀ (female rounded)"]

nets:
  N1: U1.B-IA, M4.D26
  N2: U1.B-IB, M4.D25
  N3: U1.GND, J18.pin4
  N4: U1.VCC, J18.pin3
  N5: U1.A-IA, M4.D33
  N6: U1.A-IB, M4.D32
  N7: U1.MOTOR_A-A, M2.pin_2
  N8: U1.MOTOR_A-B, M2.pin_1
  N9: U1.MOTOR_B-A, M3.pin_2
  N10: U1.MOTOR_B-B, M3.pin_1
  N11: Part2.pin_3, M4.D35
  N12: Part3.pin_1, J18.pin6
  N13: Part3.pin_2, J18.pin5
  N14: Part3.pin_3, M4.D34
  3V3: M4.3V3, Part4.VCC
  GND: M4.GND, Part4.GND
  N15: M4.D19, J18.pin8
  N16: M4.D21, J18.pin7
  N17: M4.D22, Part4.SDA
  N18: M4.D23, Part4.SCL

notes:
  GND
  VCC
  SDA
  SCL
  GY-91

custom parts:
  FC-03: FC-03, LM393 IR Speed Sensor Encoder
  DOIT Esp32 DevKit v1 (30 pins long, 11 pins width): The DOIT Esp32 DevKit v1 is one of the development board created by DOIT to evaluate the ESP-WROOM-32 module. It is based on the ESP32 microcontroller that boasts Wifi, Bluetooth, Ethernet and Low Power support all in a single chip. (vanepp) made breadboard work, adjusted pin numbering and labels and reduced size of schematic and cleaned up pcb. This chip is 30pins long (2 x15) and 11 pins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
